// Logisim project A6_20CS01044&20CS02004.circ as structural Verilog: 5 circuits, main circuit main
module main (
  input  in_1
);

  wire ADD, ADI, AND, and_1_out, ANI, clk, clock_1_out, CLR_CTR, controlunit_1_stage_1,
       controlunit_1_stage_2, controlunit_1_stage_3, controlunit_1_stage_4, controlunit_1_stage_5,
       decoder_1_out12, decoder_1_out13, decoder_1_out14, decoder_1_out15, EN_ALU, EN_IR, EN_MUX_B, EN_MUX_Y,
       EN_PC, EN_RA, EN_RB, EN_RM, EN_RY, EN_RZ, EN_Select_RA, EN_Select_RB, EN_Select_RY, HLT, LOAD, MOV,
       MVI, OR, ORI, READ_MEM, Select_MUX_B, Select_MUX_MEM, Select_MUX_Y, STOP_PC, STORE, STORE_SELECT_MUX,
       SUB, SUI, WRITE_MEM;
  wire [2:0] Select_ALU;
  wire [3:0] OPCODE, Select_RA, Select_RB, Select_RY;
  wire [15:0] MEM_IN;
  wire [31:0] adder_1_out, alu_1_alu_out, FETCH_OUT, Immediate, MEM_OUT, multiplexer_2_out,
       multiplexer_3_out, RA_q, RB_q, registerfile_1_ra, registerfile_1_rb, RM_OUT, RY, RZ_OUT;
  wire [31:16] multiplexer_1_out;

  InstructionRegister instructionregister_1 (
    .EN_IR(EN_IR), .INPUT_IR(MEM_OUT), .clk(clk), .CLR_IR(CLR_CTR), .OPCODE(OPCODE), .SELECT_RY(Select_RY),
    .SELECT_RA(Select_RA), .SELECT_RB(Select_RB), .IMMEDIATE(Immediate));
  and and_1 (and_1_out, EN_PC, ~STOP_PC);  // AND_Gate
  Multiplexer #(.width(32), .enable("false")) multiplexer_1 (
    .in0(FETCH_OUT), .in1(RZ_OUT), .out({multiplexer_1_out, MEM_IN}), .sel(Select_MUX_MEM));
  Register #(.width(32)) PC (.D(adder_1_out), .en(and_1_out), .Q(FETCH_OUT), .clk(clk), .clr(CLR_CTR));
  RAM #(.addrWidth(16), .dataWidth(32), .bus("separate")) ram_1 (
    .addr(MEM_IN), .din(RM_OUT), .data(MEM_OUT), .str(WRITE_MEM), .sel(1'b1), .clk(clk), .ld(READ_MEM),
    .clr(CLR_CTR));
  Decoder #(.select(4), .disabled(0)) decoder_1 (
    .out0(ADD), .out1(SUB), .out2(AND), .out3(OR), .out4(MOV), .out5(LOAD), .out6(STORE), .out7(MVI),
    .out8(ADI), .out9(SUI), .out10(ANI), .out11(ORI), .out12(decoder_1_out12), .out13(decoder_1_out13),
    .out14(decoder_1_out14), .out15(decoder_1_out15), .sel(OPCODE));  // open: en
  Adder #(.width(32)) adder_1 (.a(FETCH_OUT), .b(32'h1), .out(adder_1_out), .cin(in_1));  // open: cout
  or or_1 (HLT, decoder_1_out12, decoder_1_out13, decoder_1_out14, decoder_1_out15);
  or or_2 (clk, CLR_CTR, clock_1_out);
  Clock clock_1 (.out(clock_1_out));
  RegisterFile registerfile_1 (
    .RA(registerfile_1_ra), .Address_RA(Select_RA), .RB(registerfile_1_rb), .Address_RB(Select_RB), .RY(RY),
    .clk(clk), .enRA(EN_Select_RA), .enRB(EN_Select_RB), .clr(CLR_CTR), .Address_RY(Select_RY),
    .SELECT_STORE_MUX(STORE_SELECT_MUX), .enRY(EN_Select_RY));
  Register #(.width(32)) RA (.D(registerfile_1_ra), .en(EN_RA), .Q(RA_q), .clk(clk), .clr(CLR_CTR));
  Button RESET (.out(CLR_CTR));
  Register #(.width(32)) RB (.D(registerfile_1_rb), .en(EN_RB), .Q(RB_q), .clk(clk), .clr(CLR_CTR));
  ALU alu_1 (
    .ALU_Out(alu_1_alu_out), .ALU_Enable(EN_ALU), .InputRA(RA_q), .InputRB(multiplexer_2_out),
    .ALU_Select(Select_ALU));
  Register #(.width(32)) RZ (.D(alu_1_alu_out), .en(EN_RZ), .Q(RZ_OUT), .clk(clk), .clr(CLR_CTR));
  Multiplexer #(.width(32)) multiplexer_2 (
    .in0(RB_q), .in1(Immediate), .out(multiplexer_2_out), .sel(Select_MUX_B), .en(EN_MUX_B));
  // Probe on Select_ALU
  Multiplexer #(.width(32)) multiplexer_3 (
    .in0(RZ_OUT), .in1(MEM_OUT), .out(multiplexer_3_out), .sel(Select_MUX_Y), .en(EN_MUX_Y));
  Register #(.width(32)) u_RY (.D(multiplexer_3_out), .en(EN_RY), .Q(RY), .clk(clk), .clr(CLR_CTR));
  Register #(.width(32)) RM (.D(RB_q), .en(EN_RM), .Q(RM_OUT), .clk(clk), .clr(CLR_CTR));
  ControlUnit controlunit_1 (
    .EN_RA(EN_RA), .EN_RB(EN_RB), .CLR_CTR(CLR_CTR), .clk(clk), .OPCODE(OPCODE), .EN_Select_RA(EN_Select_RA),
    .ADD(ADD), .EN_Select_RB(EN_Select_RB), .ADI(ADI), .EN_ALU(EN_ALU), .SUB(SUB), .Select_ALU(Select_ALU),
    .SUI(SUI), .EN_MUX_B(EN_MUX_B), .AND(AND), .SELECT_MUX_B(Select_MUX_B), .Stage_1(controlunit_1_stage_1),
    .ANI(ANI), .EN_RZ(EN_RZ), .Stage_2(controlunit_1_stage_2), .OR(OR), .EN_RM(EN_RM),
    .Stage_3(controlunit_1_stage_3), .ORI(ORI), .EN_MUX_Y(EN_MUX_Y), .Stage_4(controlunit_1_stage_4),
    .MOV(MOV), .SELECT_MUX_Y(Select_MUX_Y), .Stage_5(controlunit_1_stage_5), .MVI(MVI),
    .EN_SELECT_RY(EN_Select_RY), .LOAD(LOAD), .SELECT_MUX_MEM(Select_MUX_MEM), .STORE(STORE), .EN_PC(EN_PC),
    .HLT(HLT), .EN_IR(EN_IR), .READ_MEM(READ_MEM), .WRITE_MEM(WRITE_MEM), .STOP_PC(STOP_PC),
    .STORE_SELECT_MUX(STORE_SELECT_MUX), .EN_RY(EN_RY));
  LED Stage_1 (.in(controlunit_1_stage_1));
  LED Stage_2 (.in(controlunit_1_stage_2));
  LED Stage_3 (.in(controlunit_1_stage_3));
  LED Stage_4 (.in(controlunit_1_stage_4));
  LED Stage_5 (.in(controlunit_1_stage_5));

  // Other names for the same wires on the sheet: CLR_IR = CLR_CTR; CLR_MEM = CLR_CTR; CLR_PC = CLR_CTR;
  //   CLR_RA = CLR_CTR; CLR_RB = CLR_CTR; CLR_RF = CLR_CTR; CLR_RM = CLR_CTR; CLR_RY = CLR_CTR; CLR_RZ = CLR_CTR

  // Notes on the sheet:
  //   FETCH UNIT
  //   MEMORY UNIT
  //   DECODE UNIT
  //   INSTRUCTION
  //   DECODER
  //   STAGE 1
  //   5 STAGE PIPELINE
  //   20CS01044 & 20CS02004
  //   Main File
endmodule

module RegisterFile (
  input  [3:0] Address_RY,
  input  enRA,
  input  enRY,
  input  [3:0] Address_RA,
  input  enRB,
  input  SELECT_STORE_MUX,
  input  [3:0] Address_RB,
  input  [31:0] RY,
  input  clk,
  input  clr,
  output [31:0] RA,
  output [31:0] RB
);

  wire R0_en, R1_en, R2_en, R3_en, R4_en, R5_en, R6_en, R7_en;
  wire [2:0] multiplexer_3_out;
  wire [3:3] multiplexer_3_out_2;
  wire [31:0] R0_out, R1_out, R2_out, R3_out, R4_out, R5_out, R6_out, R7_out;

  Demultiplexer #(.select(3), .disabled(0)) demultiplexer_1 (
    .out0(R0_en), .out1(R1_en), .out2(R2_en), .out3(R3_en), .out4(R4_en), .out5(R5_en), .out6(R6_en),
    .out7(R7_en), .in(1'b1), .sel(Address_RY[2:0]), .en(enRY));
  Register #(.width(32)) R0 (.D(RY), .en(R0_en), .Q(R0_out), .clk(clk), .clr(clr));
  Register #(.width(32)) R1 (.D(RY), .en(R1_en), .Q(R1_out), .clk(clk), .clr(clr));
  Register #(.width(32)) R2 (.D(RY), .en(R2_en), .Q(R2_out), .clk(clk), .clr(clr));
  Register #(.width(32)) R3 (.D(RY), .en(R3_en), .Q(R3_out), .clk(clk), .clr(clr));
  Register #(.width(32)) R4 (.D(RY), .en(R4_en), .Q(R4_out), .clk(clk), .clr(clr));
  Register #(.width(32)) R5 (.D(RY), .en(R5_en), .Q(R5_out), .clk(clk), .clr(clr));
  Register #(.width(32)) R6 (.D(RY), .en(R6_en), .Q(R6_out), .clk(clk), .clr(clr));
  Register #(.width(32)) R7 (.D(RY), .en(R7_en), .Q(R7_out), .clk(clk), .clr(clr));
  Multiplexer #(.select(3), .width(32)) multiplexer_1 (
    .in0(R0_out), .in1(R1_out), .in2(R2_out), .in3(R3_out), .in4(R4_out), .in5(R5_out), .in6(R6_out),
    .in7(R7_out), .out(RA), .sel(Address_RA[2:0]), .en(enRA));
  Multiplexer #(.select(3), .width(32)) multiplexer_2 (
    .in0(R0_out), .in1(R1_out), .in2(R2_out), .in3(R3_out), .in4(R4_out), .in5(R5_out), .in6(R6_out),
    .in7(R7_out), .out(RB), .sel(multiplexer_3_out), .en(enRB));
  Multiplexer #(.width(4)) multiplexer_3 (
    .in0(Address_RB), .in1(Address_RY), .out({multiplexer_3_out_2[3], multiplexer_3_out}),
    .sel(SELECT_STORE_MUX), .en(1'b1));

  // Other names for the same wires on the sheet: ADD_RY[3:0] = Address_RY

  // Notes on the sheet:
  //   20CS01044 & 20CS02004
  //   Register File
endmodule

module ALU (
  input  [31:0] InputRA,
  input  [31:0] InputRB,
  input  ALU_Enable,
  input  [2:0] ALU_Select,
  output [31:0] ALU_Out
);

  wire [31:0] Adder_out, And_out, OR_out, Subt_out;

  Adder #(.width(32)) adder_1 (.a(InputRA), .b(InputRB), .out(Adder_out), .cin(1'b0));  // open: cout
  Subtractor #(.width(32)) subtractor_1 (.a(InputRA), .b(InputRB), .out(Subt_out), .bin(1'b0));  // open: bout
  assign And_out = InputRA & InputRB;  // AND_Gate AND, 32 bits wide
  assign OR_out = InputRA | InputRB;  // OR_Gate OR, 32 bits wide
  Multiplexer #(.select(3), .width(32)) multiplexer_1 (
    .in0(Adder_out), .in1(Subt_out), .in2(And_out), .in3(OR_out), .in4(InputRA), .in5(Adder_out),
    .in6(Adder_out), .in7(InputRB), .out(ALU_Out), .sel(ALU_Select), .en(ALU_Enable));

  // Other names for the same wires on the sheet: RA[31:0] = InputRA; RB[31:0] = InputRB

  // Notes on the sheet:
  //   20CS01044 & 20CS02004
  //   Arithmetic Logic Unit
endmodule

module InstructionRegister (
  input  [31:0] INPUT_IR,
  input  EN_IR,
  input  clk,
  input  CLR_IR,
  output [3:0] OPCODE,
  output [3:0] SELECT_RA,
  output [31:0] IMMEDIATE,
  output [3:0] SELECT_RY,
  output [3:0] SELECT_RB
);

  wire [3:0] IR_q;

  Register #(.width(32)) IR (
    .D(INPUT_IR), .en(EN_IR), .Q({OPCODE, SELECT_RY, SELECT_RA, IMMEDIATE[15:0], IR_q}), .clk(clk),
    .clr(CLR_IR));

  assign IMMEDIATE[31:16] = {16{1'b0}};
  assign SELECT_RB = IMMEDIATE[15:12];

  // Notes on the sheet:
  //   20CS01044 & 20CS02004
  //   Instruction Register
endmodule

module ControlUnit (
  input  CLR_CTR,
  input  clk,
  input  [3:0] OPCODE,
  input  ADD,
  input  ADI,
  input  SUB,
  input  SUI,
  input  AND,
  input  ANI,
  input  OR,
  input  ORI,
  input  MOV,
  input  MVI,
  input  LOAD,
  input  STORE,
  input  HLT,
  output EN_RA,
  output EN_RB,
  output EN_Select_RA,
  output EN_Select_RB,
  output EN_ALU,
  output Stage_1,
  output [2:0] Select_ALU,
  output Stage_2,
  output EN_MUX_B,
  output Stage_3,
  output SELECT_MUX_B,
  output Stage_4,
  output EN_RZ,
  output Stage_5,
  output EN_RM,
  output EN_MUX_Y,
  output SELECT_MUX_Y,
  output EN_SELECT_RY,
  output SELECT_MUX_MEM,
  output EN_PC,
  output EN_IR,
  output READ_MEM,
  output WRITE_MEM,
  output STOP_PC,
  output STORE_SELECT_MUX,
  output EN_RY
);

  wire and_4_out, and_11_out, and_12_out, or_1_out, or_2_out, or_4_out, or_5_out, or_6_out, or_7_out,
       or_8_out, or_9_out, or_10_out;
  wire [2:0] counter_1_q;

  and and_1 (STORE_SELECT_MUX, Stage_2, STORE);
  and and_2 (STOP_PC, Stage_2, HLT);
  or or_1 (or_1_out, ADD, SUB, AND, OR, STORE);
  or or_2 (or_2_out, LOAD, MOV, ADI, SUI, ANI, ORI);
  Counter #(.width(3), .max('h4)) counter_1 (
    .D(3'b000), .Q(counter_1_q), .clk(clk), .clr(CLR_CTR));  // open: load, count, carry
  and and_3 (EN_RB, Stage_2, or_1_out);
  and and_4 (and_4_out, Stage_2, or_2_out);
  or or_3 (EN_RA, EN_RB, and_4_out);
  or or_4 (or_4_out, ADD, ADI, SUB, SUI, AND, ANI, ORI, MOV, MVI, LOAD, STORE, OR);
  Decoder #(.select(3), .enable("false")) decoder_1 (
    .out0(Stage_1), .out1(Stage_2), .out2(Stage_3), .out3(Stage_4), .out4(Stage_5), .sel(counter_1_q));  // open: out5, out6, out7
  and and_5 (EN_IR, Stage_1, or_4_out);
  or or_5 (or_5_out, STORE, LOAD, ADI, SUI, ANI, ORI, MVI);
  and and_6 (EN_RM, Stage_3, STORE);
  or or_6 (or_6_out, ADD, SUB, AND, MOV, OR, STORE, LOAD, ADI, SUI, ANI, ORI, MVI);
  and and_7 (EN_ALU, Stage_3, or_6_out);
  and and_8 (SELECT_MUX_B, Stage_3, or_5_out);
  or or_7 (or_7_out, STORE, LOAD);
  and and_9 (SELECT_MUX_Y, Stage_4, LOAD);
  and and_10 (WRITE_MEM, Stage_4, STORE);
  or or_8 (or_8_out, ADD, ADI, SUB, SUI, AND, ANI, OR, ORI, MOV, MVI, LOAD, STORE, HLT);
  and and_11 (and_11_out, Stage_4, LOAD);
  or or_9 (or_9_out, ADD, SUB, AND, MOV, OR, STORE, LOAD, ADI, SUI, ANI, ORI, MVI);
  or or_10 (or_10_out, ADD, SUB, AND, MOV, OR, STORE, LOAD, ADI, SUI, ANI, ORI, MVI);
  and and_12 (and_12_out, Stage_1, or_8_out);
  and and_13 (EN_MUX_Y, Stage_4, or_9_out);
  and and_14 (SELECT_MUX_MEM, Stage_4, or_7_out);
  and and_15 (EN_SELECT_RY, Stage_5, or_10_out);
  or or_11 (READ_MEM, and_12_out, and_11_out);

  assign EN_MUX_B = EN_ALU;
  assign EN_PC = EN_IR;
  assign EN_RY = EN_MUX_Y;
  assign EN_RZ = EN_ALU;
  assign EN_Select_RA = EN_RA;
  assign EN_Select_RB = EN_RB;
  assign Select_ALU = OPCODE[2:0];

  // Notes on the sheet:
  //   INSTRUCTIONS
  //   20CS01044 & 20CS02004 
  //   Control Unit
  //   STAGE 2
  //   STAGE 1
  //   STAGE COUNTER
  //   STAGE 3
  //   SIGNALS
  //   MIXED
  //   STAGE 4
  //   STAGE 5
endmodule
